# Fritzing sketch ControllerSensori (saved by Fritzing 0.8.7b)
breadboards: 1
perfboards: 1

parts:
  Componente1 = Arduino Uno (Rev3) - ICSP
  S1 = Momentary Switch [package=ksa_sealed_tac_switch]
  R1 = Resistor [tolerance=±5% resistance=220 package=THT]
  Componente2 = LCD1602-I2C
  Transceiver1 = nRF24L01 [package=module]
  LED1 = RGB LED - (4 legs) [package="5 mm [THT]"]
  R2 = Resistor [tolerance=±5% resistance=2.2k package=THT]
  R4 = Resistor [tolerance=±5% resistance=2.2k package=THT]
  R3 = Resistor [tolerance=±5% resistance=2.2k package=THT]
  buz1 = Piezo Buzzer

nets:
  N1: Componente1.A4/SDA, Componente2.SDA
  N2: Componente1.A5/SCL, Componente2.SCL
  N3: Componente1.ICSP_MISO, Componente1.D12/MISO, Transceiver1.MISO
  N4: Componente1.ICSP_MOSI, Componente1.D11_PWM/MOSI, Transceiver1.MOSI
  N5: Componente1.D9_PWM, Transceiver1.CE
  N6: Componente1.D10_PWM/SS, Transceiver1.CSN
  N7: Componente1.D13/SCK, Transceiver1.SCK
  GND: Componente1.GND, R1.Pin_1, Componente2.GND, Transceiver1.GND
  N8: Componente1.D2, buz1.pin_2
  N9: Componente1.D3_PWM, S1.4, R1.Pin_0
  N10: Componente1.D5_PWM, R4.Pin_1
  N11: Componente1.D6_PWM, R3.Pin_1
  N12: Componente1.D7, R2.Pin_1
  3V3: Componente1.3V3, Transceiver1.VCC
  5V: Componente1.5V, S1.2, Componente2.VCC, LED1.green_cathode, buz1.pin_1
  N13: LED1.red_cathode, R4.Pin_0
  N14: LED1.common_anode, R3.Pin_0
  N15: LED1.blue_cathode, R2.Pin_0

custom parts:
  LCD1602-I2C: A standard character display, usually with 2x16 characters. Comes in many colors with LCM1602 IIC attached.
  nRF24L01: nRF24L01 module
  Piezo Buzzer: Part from https://www.nutsvolts.com/magazine/article/november2012_SmileysWorkshop modified to be .3 in spacing to match the adafruit buzzer 5V breadboard friendly part.
