# Fritzing sketch ModuloParcheggio (saved by Fritzing 0.8.7b)
perfboards: 1

parts:
  Componente1 = Arduino Uno (Rev3) - ICSP
  Center = SRF05 Ultrasonic Rangefinder
  Left = SRF05 Ultrasonic Rangefinder
  Right = SRF05 Ultrasonic Rangefinder
  Transceiver1 = nRF24L01 [package=module]

nets:
  N1: Componente1.ICSP_MISO, Componente1.D12/MISO, Transceiver1.MISO
  N2: Componente1.ICSP_MOSI, Componente1.D11_PWM/MOSI, Transceiver1.MOSI
  N3: Componente1.D8, Left.Echo
  N4: Componente1.D9_PWM, Transceiver1.CE
  N5: Componente1.D10_PWM/SS, Transceiver1.CSN
  N6: Componente1.D13/SCK, Transceiver1.SCK
  N7: Componente1.D3_PWM, Right.Trig
  N8: Componente1.D4, Right.Echo
  N9: Componente1.D5_PWM, Center.Trig
  N10: Componente1.D6_PWM, Center.Echo
  N11: Componente1.D7, Left.Trig
  3V3: Componente1.3V3, Transceiver1.VCC
  VCC: Componente1.5V, Center.VCC, Left.VCC, Right.VCC
  GND: Componente1.GND, Center.GND, Left.GND, Right.GND, Transceiver1.GND

custom parts:
  nRF24L01: nRF24L01 module
