# Fritzing sketch SensoreAmbientale (saved by Fritzing 0.8.7b)
perfboards: 1

parts:
  Componente1 = Arduino Nano (Rev3.0)
  Transceiver1 = nRF24L01 [package=module]
  DHT1 = DHT11 Humitidy and Temperature Sensor (3 pins)
  R1 = PHOTOCELL [package=photocell-kit]
  R2 = Resistor [tolerance=±5% resistance=10k package=THT]

nets:
  GND: Componente1.GND, Transceiver1.GND, R2.Pin_0
  N1: Componente1.D4, DHT1.DATA
  N2: Componente1.D9, Transceiver1.CE
  N3: Componente1.D10, Transceiver1.CSN
  N4: Componente1.D11/MOSI, Transceiver1.MOSI
  N5: Componente1.D12/MISO, Transceiver1.MISO
  N6: Componente1.A6, R1.P$2
  3V3: Componente1.3V3, Transceiver1.VCC
  N7: Componente1.D13/SCK, Transceiver1.SCK

custom parts:
  nRF24L01: nRF24L01 module
  DHT11 Humitidy and Temperature Sensor (3 pins): DHT11 Humidity and Temperature Sensor (3 pins) from the design created by John De Cristofaro for Adafruit Industries.
